// Logisim project 1.circ as structural Verilog: 3 circuits, main circuit alu8
module alu8 (
  input  [11:0] a,
  input  [11:0] b,
  input  [3:0] op,
  input  sysclock,
  output [11:0] alur
);

  alu alu_1 (
    .inputa(a), .inputb(b), .operation(op), .clock(sysclock), .aluout(alur));  // open: in_5, overflow, carry, zero, out_10
endmodule

module cla (
  input  [5:0] inputa,
  input  [5:0] inputb,
  input  carryin,
  output [5:0] carryout,
  output [5:0] generator,
  output [5:0] propagator
);

  wire and_1_out, and_2_out, and_4_out, and_5_out, and_6_out, and_7_out, and_8_out, and_9_out, and_11_out,
       and_12_out, and_13_out, and_15_out, and_16_out, and_17_out, and_18_out, and_20_out, and_21_out,
       and_22_out, and_24_out, and_25_out, and_27_out;

  and and_1 (and_1_out, propagator[5], generator[4]);
  and and_2 (and_2_out, propagator[5], propagator[4], generator[3]);
  and and_3 (generator[5], inputb[5], inputa[5]);
  and and_4 (and_4_out, propagator[5], propagator[4], propagator[3], generator[2]);
  or or_1 (carryout[5], generator[5], and_1_out, and_4_out, and_5_out, and_6_out, and_2_out, and_7_out);
  xor xor_1 (propagator[5], inputb[5], inputa[5]);
  and and_5 (and_5_out, propagator[5], propagator[4], propagator[3], propagator[2], generator[1]);
  and and_6 (and_6_out, propagator[5], propagator[4], propagator[3], propagator[2], propagator[1], generator[0]);
  and and_7 (and_7_out, propagator[5], propagator[4], propagator[3], propagator[2], propagator[1], propagator[0], carryin);
  and and_8 (and_8_out, propagator[4], propagator[3], generator[2]);
  and and_9 (and_9_out, propagator[4], generator[3]);
  and and_10 (generator[4], inputb[4], inputa[4]);
  xor xor_2 (propagator[4], inputb[4], inputa[4]);
  and and_11 (and_11_out, propagator[4], propagator[3], propagator[2], generator[1]);
  or or_2 (carryout[4], generator[4], and_9_out, and_8_out, and_11_out, and_12_out, and_13_out);
  and and_12 (and_12_out, propagator[4], propagator[3], propagator[2], propagator[1], generator[0]);
  and and_13 (and_13_out, propagator[4], propagator[3], propagator[2], propagator[1], propagator[0], carryin);
  and and_14 (generator[3], inputb[3], inputa[3]);
  and and_15 (and_15_out, propagator[3], propagator[2], generator[1]);
  and and_16 (and_16_out, propagator[3], generator[2]);
  xor xor_3 (propagator[3], inputb[3], inputa[3]);
  and and_17 (and_17_out, propagator[3], propagator[2], propagator[1], generator[0]);
  and and_18 (and_18_out, propagator[3], propagator[2], propagator[1], propagator[0], carryin);
  or or_3 (carryout[3], generator[3], and_16_out, and_15_out, and_17_out, and_18_out);
  and and_19 (generator[2], inputb[2], inputa[2]);
  and and_20 (and_20_out, generator[1], propagator[2]);
  or or_4 (carryout[2], generator[2], and_20_out, and_22_out, and_21_out);
  xor xor_4 (propagator[2], inputb[2], inputa[2]);
  and and_21 (and_21_out, propagator[2], propagator[1], propagator[0], carryin);
  and and_22 (and_22_out, generator[0], propagator[2], propagator[1]);
  xor xor_5 (propagator[1], inputb[1], inputa[1]);
  and and_23 (generator[1], inputb[1], inputa[1]);
  and and_24 (and_24_out, carryin, propagator[1], propagator[0]);
  and and_25 (and_25_out, generator[0], propagator[1]);
  or or_5 (carryout[1], generator[1], and_25_out, and_24_out);
  and and_26 (generator[0], inputb[0], inputa[0]);
  xor xor_6 (propagator[0], inputb[0], inputa[0]);
  and and_27 (and_27_out, carryin, propagator[0]);
  or or_6 (carryout[0], generator[0], and_27_out);

  // Other names for the same wires on the sheet: c0 = carryout[0]; c1 = carryout[1]; c2 = carryout[2];
  //   c3 = carryout[3]; c4 = carryout[4]; c5 = carryout[5]; ci = carryin; g0 = generator[0]; g1 = generator[1];
  //   g2 = generator[2]; g3 = generator[3]; g4 = generator[4]; g5 = generator[5]; pz = propagator[0];
  //   p1 = propagator[1]; p2 = propagator[2]; p3 = propagator[3]; p4 = propagator[4]; p5 = propagator[5]
endmodule

module alu (
  input  [11:0] inputa,
  input  [11:0] inputb,
  input  [3:0] operation,
  input  clock,
  input  in_5,
  output [11:0] aluout,
  output overflow,
  output carry,
  output zero,
  output out_10
);

  wire and_2_out, and_5_out, and_6_out, and_7_out, and_8_out, and_9_out, and_10_out, and_11_out, C, c_t, clk,
       d0, d1, d2, d3, d4, d5, d6, d7, d8, d9, d10, d11, msk, nand_1_out, nand_2_out, not_1_out, ovr_flag,
       S0, s0_t, S1, s1_t, S2, s2_t, S3, s3_t, S4, s4_t, S5, s5_t, se0, se1, se2;
  wire [4:0] cla_1_carryout, cla_2_carryout;
  wire [5:0] cla_1_propagator, cla_2_propagator, xor_1_out, xor_2_out;
  wire [11:0] and_3_out, multiplexer_1_out, or_2_out, register_1_q, xor_3_out;
  wire [11:11] not_2_out;

  or or_1 (msk, ~operation[2], operation[1], operation[3]);  // OR_Gate
  nand nand_1 (nand_1_out, ~operation[3], operation[2], operation[1], ~operation[0]);  // NAND_Gate
  nand nand_2 (nand_2_out, ~operation[3], operation[2], operation[1], operation[0]);  // NAND_Gate
  assign xor_1_out = {6{operation[0]}} ^ inputb[11:6];  // XOR_Gate xor_1, 6 bits wide
  Multiplexer #(.width(12), .enable("false")) multiplexer_1 (
    .in0(xor_3_out), .in1({{11{operation[0]}}, out_10}), .out(multiplexer_1_out), .sel(operation[3]));
  and and_1 (clk, clock, and_2_out);
  and and_2 (and_2_out, nand_1_out, nand_2_out);
  assign xor_2_out = {6{operation[0]}} ^ inputb[5:0];  // XOR_Gate xor_2, 6 bits wide
  assign xor_3_out = inputa ^ {d11, d10, d9, d8, d7, d6, d5, d4, d3, d2, d1, d0};  // XOR_Gate xor_3, 12 bits wide
  nor nor_1 (out_10, xor_3_out[11], xor_3_out[10], xor_3_out[9], xor_3_out[8], xor_3_out[7], xor_3_out[6], xor_3_out[5], xor_3_out[4], xor_3_out[3], xor_3_out[2], xor_3_out[1], xor_3_out[0]);
  assign and_3_out = inputa & inputb;  // AND_Gate and_3, 12 bits wide
  assign or_2_out = inputa | inputb;  // OR_Gate or_2, 12 bits wide
  not not_1 (not_1_out, msk);
  Multiplexer #(.select(3), .width(12), .enable("false")) multiplexer_2 (
    .in0({S5, S4, S3, S2, S1, S0, s5_t, s4_t, s3_t, s2_t, s1_t, s0_t}), .in1(and_3_out), .in2(or_2_out),
    .in3(multiplexer_1_out), .in4(inputa), .in5(register_1_q), .in6({inputa[10:0], operation[1]}),
    .in7({operation[1], inputa[11:1]}), .out(aluout), .sel({se2, se1, se0}));
  Register #(.width(12)) register_1 (
    .D({{9{in_5}}, overflow, carry, zero}), .clk(clk), .Q(register_1_q));  // open: en, clr
  and and_4 (overflow, not_1_out, ovr_flag);
  and and_5 (and_5_out, ~operation[2], ~operation[0]);  // AND_Gate
  and and_6 (and_6_out, ~operation[2], operation[1]);  // AND_Gate
  and and_7 (and_7_out, ~operation[2], ~operation[1]);  // AND_Gate
  and and_8 (and_8_out, operation[3], operation[0]);
  and and_9 (and_9_out, operation[2], operation[1], operation[0]);
  nor nor_2 (zero, aluout[1], aluout[2], aluout[3], aluout[4], aluout[5], aluout[6], aluout[7], aluout[8], aluout[9], aluout[10], aluout[11], aluout[0]);
  and and_10 (and_10_out, operation[2], operation[1]);
  and and_11 (and_11_out, operation[3], ~operation[1]);  // AND_Gate
  or or_3 (se1, and_5_out, and_6_out, operation[3]);
  cla cla_1 (
    .inputa(inputa[5:0]), .inputb(xor_2_out), .carryin(operation[0]), .carryout({c_t, cla_1_carryout}),
    .propagator(cla_1_propagator));  // open: generator
  cla cla_2 (
    .inputa(inputa[11:6]), .inputb(xor_1_out), .carryin(c_t), .carryout({C, cla_2_carryout}),
    .propagator(cla_2_propagator));  // open: generator
  or or_4 (se2, and_10_out, and_11_out);
  or or_5 (se0, and_5_out, and_7_out, and_8_out, and_9_out);
  xor xor_4 (ovr_flag, C, cla_2_carryout[4]);
  Multiplexer #(.width(12), .enable("false")) multiplexer_3 (
    .in0(inputb), .in1({12{not_2_out[11]}}), .out({d11, d10, d9, d8, d7, d6, d5, d4, d3, d2, d1, d0}),
    .sel(not_2_out[11]));
  not not_2 (not_2_out[11], operation[1]);
  assign {s5_t, s4_t, s3_t, s2_t, s1_t, s0_t} = {cla_1_carryout, operation[0]} ^ cla_1_propagator;  // XOR_Gate xor_5, 6 bits wide
  assign {S5, S4, S3, S2, S1, S0} = {cla_2_carryout, c_t} ^ cla_2_propagator;  // XOR_Gate xor_6, 6 bits wide
  and and_12 (carry, not_1_out, C);

  // Other names for the same wires on the sheet: f1 = operation[1]; a0 = inputa[0]; a1 = inputa[1]; a2 = inputa[2];
  //   a3 = inputa[3]; a4 = inputa[4]; a5 = inputa[5]; a6 = inputa[6]; a7 = inputa[7]; a8 = inputa[8]; a9 = inputa[9];
  //   a10 = inputa[10]; a11 = inputa[11]; al1 = aluout[0]; al2 = aluout[1]; al3 = aluout[2]; al4 = aluout[3];
  //   al5 = aluout[4]; al6 = aluout[5]; al7 = aluout[6]; al8 = aluout[7]; al9 = aluout[8]; al10 = aluout[9];
  //   al11 = aluout[10]; al12 = aluout[11]; ovr = overflow; b0 = inputb[0]; b1 = inputb[1]; b2 = inputb[2];
  //   b3 = inputb[3]; b4 = inputb[4]; b5 = inputb[5]; b6 = inputb[6]; b7 = inputb[7]; b8 = inputb[8]; b9 = inputb[9];
  //   b10 = inputb[10]; b11 = inputb[11]; f0 = operation[0]; m = operation[0]; f2 = operation[2]; f3 = operation[3]
endmodule
