// Logisim project 2.circ as structural Verilog: 1 circuit, main circuit instructions
module instructions (
  input  resetall,
  input  sysclock,
  input  jmp,
  input  [11:0] a,
  output [11:0] pc,
  output [3:0] op,
  output [2:0] rd,
  output [2:0] rs1,
  output [2:0] rs2,
  output [11:0] imm
);

  wire and_1_out, and_2_out, and_4_out, and_5_out, and_6_out, and_7_out, and_8_out, and_9_out, and_10_out,
       and_11_out, and_12_out, multiplexer_1_out, multiplexer_2_out, multiplexer_3_out, multiplexer_4_out,
       multiplexer_5_out, multiplexer_6_out, multiplexer_7_out, multiplexer_8_out, multiplexer_9_out,
       multiplexer_10_out, multiplexer_11_out, multiplexer_12_out, xor_1_out, xor_2_out, xor_3_out,
       xor_4_out, xor_5_out, xor_6_out, xor_7_out, xor_8_out, xor_9_out, xor_10_out, xor_11_out, xor_12_out;

  Multiplexer #(.enable("false")) multiplexer_1 (.in0(xor_2_out), .in1(a[3]), .out(multiplexer_1_out), .sel(jmp));
  Multiplexer #(.enable("false")) multiplexer_2 (.in0(xor_3_out), .in1(a[7]), .out(multiplexer_2_out), .sel(jmp));
  Multiplexer #(.enable("false")) multiplexer_3 (.in0(xor_1_out), .in1(a[11]), .out(multiplexer_3_out), .sel(jmp));
  and and_1 (and_1_out, and_4_out, pc[3]);
  D_Flip_Flop d_ff_1 (.D(multiplexer_1_out), .clk(sysclock), .Q(pc[3]), .reset(resetall));  // open: Qn, preset
  and and_2 (and_2_out, and_5_out, pc[7]);
  D_Flip_Flop d_ff_2 (.D(multiplexer_2_out), .clk(sysclock), .Q(pc[7]), .reset(resetall));  // open: Qn, preset
  // AND_Gate and_3 has open pins: in0=and_6_out, in1=pc[11], out=open
  xor xor_1 (xor_1_out, and_6_out, pc[11]);
  D_Flip_Flop d_ff_3 (.D(multiplexer_3_out), .clk(sysclock), .Q(pc[11]), .reset(resetall));  // open: Qn, preset
  xor xor_2 (xor_2_out, and_4_out, pc[3]);
  xor xor_3 (xor_3_out, and_5_out, pc[7]);
  Multiplexer #(.enable("false")) multiplexer_4 (.in0(xor_5_out), .in1(a[2]), .out(multiplexer_4_out), .sel(jmp));
  Multiplexer #(.enable("false")) multiplexer_5 (.in0(xor_4_out), .in1(a[10]), .out(multiplexer_5_out), .sel(jmp));
  and and_4 (and_4_out, and_7_out, pc[2]);
  D_Flip_Flop d_ff_4 (.D(multiplexer_4_out), .clk(sysclock), .Q(pc[2]), .reset(resetall));  // open: Qn, preset
  and and_5 (and_5_out, and_9_out, pc[6]);
  Multiplexer #(.enable("false")) multiplexer_6 (.in0(xor_6_out), .in1(a[6]), .out(multiplexer_6_out), .sel(jmp));
  D_Flip_Flop d_ff_5 (.D(multiplexer_6_out), .clk(sysclock), .Q(pc[6]), .reset(resetall));  // open: Qn, preset
  and and_6 (and_6_out, and_8_out, pc[10]);
  xor xor_4 (xor_4_out, and_8_out, pc[10]);
  D_Flip_Flop d_ff_6 (.D(multiplexer_5_out), .clk(sysclock), .Q(pc[10]), .reset(resetall));  // open: Qn, preset
  RAM #(.addrWidth(12), .dataWidth(25)) ram_1 (
    .addr(pc), .we(1'b0), .oe(1'b1), .clk(sysclock), .data({op, rd, rs1, rs2, imm}));
  xor xor_5 (xor_5_out, and_7_out, pc[2]);
  xor xor_6 (xor_6_out, and_9_out, pc[6]);
  and and_7 (and_7_out, and_10_out, pc[1]);
  Multiplexer #(.enable("false")) multiplexer_7 (.in0(xor_7_out), .in1(a[1]), .out(multiplexer_7_out), .sel(jmp));
  Multiplexer #(.enable("false")) multiplexer_8 (.in0(xor_8_out), .in1(a[5]), .out(multiplexer_8_out), .sel(jmp));
  and and_8 (and_8_out, and_11_out, pc[9]);
  Multiplexer #(.enable("false")) multiplexer_9 (.in0(xor_9_out), .in1(a[9]), .out(multiplexer_9_out), .sel(jmp));
  D_Flip_Flop d_ff_7 (.D(multiplexer_9_out), .clk(sysclock), .Q(pc[9]), .reset(resetall));  // open: Qn, preset
  xor xor_7 (xor_7_out, and_10_out, pc[1]);
  D_Flip_Flop d_ff_8 (.D(multiplexer_7_out), .clk(sysclock), .Q(pc[1]), .reset(resetall));  // open: Qn, preset
  and and_9 (and_9_out, and_12_out, pc[5]);
  xor xor_8 (xor_8_out, and_12_out, pc[5]);
  D_Flip_Flop d_ff_9 (.D(multiplexer_8_out), .clk(sysclock), .Q(pc[5]), .reset(resetall));  // open: Qn, preset
  xor xor_9 (xor_9_out, and_11_out, pc[9]);
  and and_10 (and_10_out, 1'b1, pc[0]);
  Multiplexer #(.enable("false")) multiplexer_10 (.in0(xor_10_out), .in1(a[0]), .out(multiplexer_10_out), .sel(jmp));
  Multiplexer #(.enable("false")) multiplexer_11 (.in0(xor_11_out), .in1(a[4]), .out(multiplexer_11_out), .sel(jmp));
  and and_11 (and_11_out, and_2_out, pc[8]);
  Multiplexer #(.enable("false")) multiplexer_12 (.in0(xor_12_out), .in1(a[8]), .out(multiplexer_12_out), .sel(jmp));
  D_Flip_Flop d_ff_10 (.D(multiplexer_12_out), .clk(sysclock), .Q(pc[8]), .reset(resetall));  // open: Qn, preset
  xor xor_10 (xor_10_out, 1'b1, pc[0]);
  D_Flip_Flop d_ff_11 (.D(multiplexer_10_out), .clk(sysclock), .Q(pc[0]), .reset(resetall));  // open: Qn, preset
  and and_12 (and_12_out, and_1_out, pc[4]);
  xor xor_11 (xor_11_out, and_1_out, pc[4]);
  D_Flip_Flop d_ff_12 (.D(multiplexer_11_out), .clk(sysclock), .Q(pc[4]), .reset(resetall));  // open: Qn, preset
  xor xor_12 (xor_12_out, and_2_out, pc[8]);

  // Other names for the same wires on the sheet: clk = sysclock; im0 = imm[0]; im1 = imm[1]; im2 = imm[2];
  //   im3 = imm[3]; im4 = imm[4]; im5 = imm[5]; im6 = imm[6]; im7 = imm[7]; im8 = imm[8]; im9 = imm[9];
  //   im10 = imm[10]; im11 = imm[11]; sc = resetall
endmodule
