// Logisim project 3.circ as structural Verilog: 1 circuit, main circuit regfile
module regfile (
  input  [2:0] rd,
  input  [11:0] alur,
  input  [11:0] pc,
  input  [11:0] imm,
  input  [3:0] op,
  input  wen,
  input  resetall,
  input  sysclock,
  output [11:0] x0,
  output [11:0] x1,
  output [11:0] x2,
  output [11:0] x3,
  output [11:0] x4,
  output [11:0] x5,
  output [11:0] x6,
  output [11:0] x7
);

  wire demultiplexer_1_out0, demultiplexer_1_out1, demultiplexer_1_out2, demultiplexer_1_out3,
       demultiplexer_1_out4, demultiplexer_1_out5, demultiplexer_1_out6, demultiplexer_1_out7, reg0, reg1,
       reg2, reg3, reg4, reg5, reg6, reg7, s0, s1;
  wire [11:0] mux;

  Register #(.width(12)) register_1 (.D(mux), .en(demultiplexer_1_out0), .clk(reg0), .Q(x0), .clr(resetall));
  Register #(.width(12)) register_2 (.D(mux), .en(demultiplexer_1_out1), .clk(reg1), .Q(x1), .clr(resetall));
  Register #(.width(12)) register_3 (.D(mux), .en(demultiplexer_1_out2), .clk(reg2), .Q(x2), .clr(resetall));
  Register #(.width(12)) register_4 (.D(mux), .en(demultiplexer_1_out3), .clk(reg3), .Q(x3), .clr(resetall));
  Register #(.width(12)) register_5 (.D(mux), .en(demultiplexer_1_out4), .clk(reg4), .Q(x4), .clr(resetall));
  Register #(.width(12)) register_6 (.D(mux), .en(demultiplexer_1_out5), .clk(reg5), .Q(x5), .clr(resetall));
  Register #(.width(12)) register_7 (.D(mux), .en(demultiplexer_1_out6), .clk(reg6), .Q(x6), .clr(resetall));
  Register #(.width(12)) register_8 (.D(mux), .en(demultiplexer_1_out7), .clk(reg7), .Q(x7), .clr(resetall));
  and and_1 (s1, op[3], ~op[2], op[0]);  // AND_Gate
  and and_2 (reg0, ~rd[0], ~rd[1], ~rd[2], sysclock);  // AND_Gate
  and and_3 (reg1, rd[0], ~rd[1], ~rd[2], sysclock);  // AND_Gate
  and and_4 (reg2, ~rd[0], rd[1], ~rd[2], sysclock);  // AND_Gate
  and and_5 (s0, op[3], ~op[2], ~op[1], ~op[0]);  // AND_Gate
  and and_6 (reg3, rd[0], rd[1], ~rd[2], sysclock);  // AND_Gate
  and and_7 (reg4, ~rd[0], ~rd[1], rd[2], sysclock);  // AND_Gate
  and and_8 (reg5, rd[0], ~rd[1], rd[2], sysclock);  // AND_Gate
  Demultiplexer #(.select(3), .enable("false")) demultiplexer_1 (
    .out0(demultiplexer_1_out0), .out1(demultiplexer_1_out1), .out2(demultiplexer_1_out2),
    .out3(demultiplexer_1_out3), .out4(demultiplexer_1_out4), .out5(demultiplexer_1_out5),
    .out6(demultiplexer_1_out6), .out7(demultiplexer_1_out7), .in(wen), .sel(rd));
  Multiplexer #(.select(2), .width(12), .enable("false")) multiplexer_1 (
    .in0(alur), .in1(pc), .in2(imm), .out(mux), .sel({s1, s0}));  // open: in3
  and and_9 (reg6, ~rd[0], rd[1], rd[2], sysclock);  // AND_Gate
  and and_10 (reg7, rd[0], rd[1], rd[2], sysclock);

  // Other names for the same wires on the sheet: clk = sysclock; D = op[0]; C = op[1]; B = op[2]; A = op[3];
  //   q0[11:0] = x0; q1[11:0] = x1; q2[11:0] = x2; q3[11:0] = x3; q4[11:0] = x4; q5[11:0] = x5; q6[11:0] = x6;
  //   q7[11:0] = x7
endmodule
