// Logisim project 4.circ as structural Verilog: 6 circuits, main circuit cpu
module cpu (
  input  resetall,
  input  sysclock,
  output [11:0] pc,
  output [11:0] x0,
  output [11:0] x1,
  output [11:0] x2,
  output [11:0] x3,
  output [11:0] x4,
  output [11:0] x5,
  output [11:0] x6,
  output [11:0] x7
);

  wire and_1_out, and_2_out, and_3_out, and_5_out, d_ff_1_q, d_ff_2_q, d_ff_3_q, jmp, multiplexer_1_out,
       multiplexer_2_out, multiplexer_5_out, or_1_out;
  wire [2:0] rd, rs1, rs2;
  wire [3:0] op;
  wire [11:0] A, alu8_1_alur, imm, multiplexer_4_out;

  Multiplexer #(.enable("false")) multiplexer_1 (.in0(sysclock), .in1(1'b0), .out(multiplexer_1_out), .sel(d_ff_1_q));
  and and_1 (and_1_out, op[0], op[1], op[2], op[3]);
  D_Flip_Flop d_ff_1 (.D(and_1_out), .clk(and_1_out), .Q(d_ff_1_q));  // open: Qn, preset, reset
  Multiplexer #(.enable("false")) multiplexer_2 (.in0(jmp), .in1(1'b0), .out(multiplexer_2_out), .sel(d_ff_2_q));
  and and_2 (and_2_out, ~op[0], op[1], op[2], op[3]);  // AND_Gate
  D_Flip_Flop d_ff_2 (.D(and_2_out), .clk(and_2_out), .Q(d_ff_2_q), .reset(resetall));  // open: Qn, preset
  Multiplexer #(.select(3), .width(12), .enable("false")) multiplexer_3 (
    .in0(x0), .in1(x1), .in2(x2), .in3(x3), .in4(x4), .in5(x5), .in6(x6), .in7(x7), .out(A), .sel(rs1));
  instructions instructions_1 (
    .resetall(resetall), .sysclock(multiplexer_1_out), .jmp(multiplexer_2_out), .a(A), .pc(pc), .op(op),
    .rd(rd), .rs1(rs1), .rs2(rs2), .imm(imm));
  Multiplexer #(.select(3), .width(12), .enable("false")) multiplexer_4 (
    .in0(x0), .in1(x1), .in2(x2), .in3(x3), .in4(x4), .in5(x5), .in6(x6), .in7(x7), .out(multiplexer_4_out),
    .sel(rs2));
  alu8 alu8_1 (.a(A), .b(multiplexer_4_out), .op(op), .sysclock(sysclock), .alur(alu8_1_alur));
  and and_3 (and_3_out, ~op[0], ~op[2]);  // AND_Gate
  and and_4 (jmp, op[0], op[1], ~op[2], op[3]);  // AND_Gate
  or or_1 (or_1_out, ~op[1], ~op[3], and_3_out);  // OR_Gate
  Multiplexer #(.enable("false")) multiplexer_5 (.in0(sysclock), .in1(1'b0), .out(multiplexer_5_out), .sel(d_ff_3_q));
  and and_5 (and_5_out, ~op[0], op[1], op[2], op[3]);  // AND_Gate
  regfile regfile_1 (
    .rd(rd), .alur(alu8_1_alur), .pc(pc), .imm(imm), .op(op), .wen(or_1_out), .resetall(resetall),
    .sysclock(multiplexer_5_out), .x0(x0), .x1(x1), .x2(x2), .x3(x3), .x4(x4), .x5(x5), .x6(x6), .x7(x7));
  D_Flip_Flop d_ff_3 (.D(and_5_out), .clk(and_5_out), .Q(d_ff_3_q), .reset(resetall));  // open: Qn, preset
endmodule

module alu8 (
  input  [11:0] a,
  input  [11:0] b,
  input  [3:0] op,
  input  sysclock,
  output [11:0] alur
);

  alu alu_1 (
    .inputa(a), .inputb(b), .operation(op), .clock(sysclock), .aluout(alur));  // open: in_5, overflow, carry, zero, out_10
endmodule

module cla (
  input  [5:0] inputa,
  input  [5:0] inputb,
  input  carryin,
  output [5:0] carryout,
  output [5:0] generator,
  output [5:0] propagator
);

  wire and_1_out, and_2_out, and_4_out, and_5_out, and_6_out, and_7_out, and_8_out, and_9_out, and_11_out,
       and_12_out, and_13_out, and_15_out, and_16_out, and_17_out, and_18_out, and_20_out, and_21_out,
       and_22_out, and_24_out, and_25_out, and_27_out;

  and and_1 (and_1_out, propagator[5], generator[4]);
  and and_2 (and_2_out, propagator[5], propagator[4], generator[3]);
  and and_3 (generator[5], inputb[5], inputa[5]);
  and and_4 (and_4_out, propagator[5], propagator[4], propagator[3], generator[2]);
  or or_1 (carryout[5], generator[5], and_1_out, and_4_out, and_5_out, and_6_out, and_2_out, and_7_out);
  xor xor_1 (propagator[5], inputb[5], inputa[5]);
  and and_5 (and_5_out, propagator[5], propagator[4], propagator[3], propagator[2], generator[1]);
  and and_6 (and_6_out, propagator[5], propagator[4], propagator[3], propagator[2], propagator[1], generator[0]);
  and and_7 (and_7_out, propagator[5], propagator[4], propagator[3], propagator[2], propagator[1], propagator[0], carryin);
  and and_8 (and_8_out, propagator[4], generator[3]);
  and and_9 (and_9_out, propagator[4], propagator[3], generator[2]);
  and and_10 (generator[4], inputb[4], inputa[4]);
  xor xor_2 (propagator[4], inputb[4], inputa[4]);
  and and_11 (and_11_out, propagator[4], propagator[3], propagator[2], generator[1]);
  or or_2 (carryout[4], generator[4], and_8_out, and_9_out, and_11_out, and_12_out, and_13_out);
  and and_12 (and_12_out, propagator[4], propagator[3], propagator[2], propagator[1], generator[0]);
  and and_13 (and_13_out, propagator[4], propagator[3], propagator[2], propagator[1], propagator[0], carryin);
  and and_14 (generator[3], inputb[3], inputa[3]);
  and and_15 (and_15_out, propagator[3], generator[2]);
  and and_16 (and_16_out, propagator[3], propagator[2], generator[1]);
  xor xor_3 (propagator[3], inputb[3], inputa[3]);
  and and_17 (and_17_out, propagator[3], propagator[2], propagator[1], propagator[0], carryin);
  and and_18 (and_18_out, propagator[3], propagator[2], propagator[1], generator[0]);
  or or_3 (carryout[3], generator[3], and_15_out, and_16_out, and_18_out, and_17_out);
  and and_19 (generator[2], inputb[2], inputa[2]);
  and and_20 (and_20_out, generator[1], propagator[2]);
  or or_4 (carryout[2], generator[2], and_20_out, and_21_out, and_22_out);
  xor xor_4 (propagator[2], inputb[2], inputa[2]);
  and and_21 (and_21_out, generator[0], propagator[2], propagator[1]);
  and and_22 (and_22_out, propagator[2], propagator[1], propagator[0], carryin);
  xor xor_5 (propagator[1], inputb[1], inputa[1]);
  and and_23 (generator[1], inputb[1], inputa[1]);
  and and_24 (and_24_out, generator[0], propagator[1]);
  and and_25 (and_25_out, carryin, propagator[1], propagator[0]);
  or or_5 (carryout[1], generator[1], and_24_out, and_25_out);
  and and_26 (generator[0], inputb[0], inputa[0]);
  xor xor_6 (propagator[0], inputb[0], inputa[0]);
  and and_27 (and_27_out, carryin, propagator[0]);
  or or_6 (carryout[0], generator[0], and_27_out);

  // Other names for the same wires on the sheet: c0 = carryout[0]; c1 = carryout[1]; c2 = carryout[2];
  //   c3 = carryout[3]; c4 = carryout[4]; c5 = carryout[5]; ci = carryin; g0 = generator[0]; g1 = generator[1];
  //   g2 = generator[2]; g3 = generator[3]; g4 = generator[4]; g5 = generator[5]; pz = propagator[0];
  //   p1 = propagator[1]; p2 = propagator[2]; p3 = propagator[3]; p4 = propagator[4]; p5 = propagator[5]
endmodule

module alu (
  input  [11:0] inputa,
  input  [11:0] inputb,
  input  [3:0] operation,
  input  clock,
  input  in_5,
  output [11:0] aluout,
  output overflow,
  output carry,
  output zero,
  output out_10
);

  wire and_2_out, and_5_out, and_6_out, and_7_out, and_8_out, and_9_out, and_10_out, and_11_out, C, c_t, clk,
       d0, d1, d2, d3, d4, d5, d6, d7, d8, d9, d10, d11, msk, nand_1_out, nand_2_out, not_1_out, ovr_flag,
       S0, s0_t, S1, s1_t, S2, s2_t, S3, s3_t, S4, s4_t, S5, s5_t, se0, se1, se2;
  wire [4:0] cla_1_carryout, cla_2_carryout;
  wire [5:0] cla_1_propagator, cla_2_propagator, xor_1_out, xor_2_out;
  wire [11:0] and_3_out, multiplexer_1_out, or_2_out, register_1_q, xor_3_out;
  wire [11:11] not_2_out;

  or or_1 (msk, ~operation[2], operation[1], operation[3]);  // OR_Gate
  nand nand_1 (nand_1_out, ~operation[3], operation[2], operation[1], ~operation[0]);  // NAND_Gate
  nand nand_2 (nand_2_out, ~operation[3], operation[2], operation[1], operation[0]);  // NAND_Gate
  assign xor_1_out = {6{operation[0]}} ^ inputb[11:6];  // XOR_Gate xor_1, 6 bits wide
  Multiplexer #(.width(12), .enable("false")) multiplexer_1 (
    .in0(xor_3_out), .in1({{11{operation[0]}}, out_10}), .out(multiplexer_1_out), .sel(operation[3]));
  and and_1 (clk, clock, and_2_out);
  and and_2 (and_2_out, nand_1_out, nand_2_out);
  assign xor_2_out = {6{operation[0]}} ^ inputb[5:0];  // XOR_Gate xor_2, 6 bits wide
  assign xor_3_out = inputa ^ {d11, d10, d9, d8, d7, d6, d5, d4, d3, d2, d1, d0};  // XOR_Gate xor_3, 12 bits wide
  nor nor_1 (out_10, xor_3_out[11], xor_3_out[10], xor_3_out[9], xor_3_out[8], xor_3_out[7], xor_3_out[6], xor_3_out[5], xor_3_out[4], xor_3_out[3], xor_3_out[2], xor_3_out[1], xor_3_out[0]);
  assign and_3_out = inputa & inputb;  // AND_Gate and_3, 12 bits wide
  assign or_2_out = inputa | inputb;  // OR_Gate or_2, 12 bits wide
  not not_1 (not_1_out, msk);
  Multiplexer #(.select(3), .width(12), .enable("false")) multiplexer_2 (
    .in0({S5, S4, S3, S2, S1, S0, s5_t, s4_t, s3_t, s2_t, s1_t, s0_t}), .in1(and_3_out), .in2(or_2_out),
    .in3(multiplexer_1_out), .in4(inputa), .in5(register_1_q), .in6({inputa[10:0], operation[1]}),
    .in7({operation[1], inputa[11:1]}), .out(aluout), .sel({se2, se1, se0}));
  Register #(.width(12)) register_1 (
    .D({{9{in_5}}, overflow, carry, zero}), .clk(clk), .Q(register_1_q));  // open: en, clr
  and and_4 (overflow, not_1_out, ovr_flag);
  and and_5 (and_5_out, ~operation[2], ~operation[0]);  // AND_Gate
  and and_6 (and_6_out, ~operation[2], operation[1]);  // AND_Gate
  and and_7 (and_7_out, ~operation[2], ~operation[1]);  // AND_Gate
  and and_8 (and_8_out, operation[3], operation[0]);
  and and_9 (and_9_out, operation[2], operation[1], operation[0]);
  nor nor_2 (zero, aluout[1], aluout[2], aluout[3], aluout[4], aluout[5], aluout[6], aluout[7], aluout[8], aluout[9], aluout[10], aluout[11], aluout[0]);
  and and_10 (and_10_out, operation[2], operation[1]);
  and and_11 (and_11_out, operation[3], ~operation[1]);  // AND_Gate
  or or_3 (se1, and_5_out, and_6_out, operation[3]);
  cla cla_1 (
    .inputa(inputa[5:0]), .inputb(xor_2_out), .carryin(operation[0]), .carryout({c_t, cla_1_carryout}),
    .propagator(cla_1_propagator));  // open: generator
  cla cla_2 (
    .inputa(inputa[11:6]), .inputb(xor_1_out), .carryin(c_t), .carryout({C, cla_2_carryout}),
    .propagator(cla_2_propagator));  // open: generator
  or or_4 (se2, and_10_out, and_11_out);
  or or_5 (se0, and_5_out, and_7_out, and_8_out, and_9_out);
  xor xor_4 (ovr_flag, C, cla_2_carryout[4]);
  Multiplexer #(.width(12), .enable("false")) multiplexer_3 (
    .in0(inputb), .in1({12{not_2_out[11]}}), .out({d11, d10, d9, d8, d7, d6, d5, d4, d3, d2, d1, d0}),
    .sel(not_2_out[11]));
  not not_2 (not_2_out[11], operation[1]);
  assign {s5_t, s4_t, s3_t, s2_t, s1_t, s0_t} = {cla_1_carryout, operation[0]} ^ cla_1_propagator;  // XOR_Gate xor_5, 6 bits wide
  assign {S5, S4, S3, S2, S1, S0} = {cla_2_carryout, c_t} ^ cla_2_propagator;  // XOR_Gate xor_6, 6 bits wide
  and and_12 (carry, not_1_out, C);

  // Other names for the same wires on the sheet: f1 = operation[1]; a0 = inputa[0]; a1 = inputa[1]; a2 = inputa[2];
  //   a3 = inputa[3]; a4 = inputa[4]; a5 = inputa[5]; a6 = inputa[6]; a7 = inputa[7]; a8 = inputa[8]; a9 = inputa[9];
  //   a10 = inputa[10]; a11 = inputa[11]; al1 = aluout[0]; al2 = aluout[1]; al3 = aluout[2]; al4 = aluout[3];
  //   al5 = aluout[4]; al6 = aluout[5]; al7 = aluout[6]; al8 = aluout[7]; al9 = aluout[8]; al10 = aluout[9];
  //   al11 = aluout[10]; al12 = aluout[11]; ovr = overflow; b0 = inputb[0]; b1 = inputb[1]; b2 = inputb[2];
  //   b3 = inputb[3]; b4 = inputb[4]; b5 = inputb[5]; b6 = inputb[6]; b7 = inputb[7]; b8 = inputb[8]; b9 = inputb[9];
  //   b10 = inputb[10]; b11 = inputb[11]; f0 = operation[0]; m = operation[0]; f2 = operation[2]; f3 = operation[3]
endmodule

module instructions (
  input  resetall,
  input  sysclock,
  input  jmp,
  input  [11:0] a,
  output [11:0] pc,
  output [3:0] op,
  output [2:0] rd,
  output [2:0] rs1,
  output [2:0] rs2,
  output [11:0] imm
);

  wire and_1_out, and_2_out, and_4_out, and_5_out, and_6_out, and_7_out, and_8_out, and_9_out, and_10_out,
       and_11_out, and_12_out, multiplexer_1_out, multiplexer_2_out, multiplexer_3_out, multiplexer_4_out,
       multiplexer_5_out, multiplexer_6_out, multiplexer_7_out, multiplexer_8_out, multiplexer_9_out,
       multiplexer_10_out, multiplexer_11_out, multiplexer_12_out, xor_1_out, xor_2_out, xor_3_out,
       xor_4_out, xor_5_out, xor_6_out, xor_7_out, xor_8_out, xor_9_out, xor_10_out, xor_11_out, xor_12_out;

  Multiplexer #(.enable("false")) multiplexer_1 (.in0(xor_2_out), .in1(a[3]), .out(multiplexer_1_out), .sel(jmp));
  Multiplexer #(.enable("false")) multiplexer_2 (.in0(xor_3_out), .in1(a[7]), .out(multiplexer_2_out), .sel(jmp));
  Multiplexer #(.enable("false")) multiplexer_3 (.in0(xor_1_out), .in1(a[11]), .out(multiplexer_3_out), .sel(jmp));
  and and_1 (and_1_out, and_4_out, pc[3]);
  D_Flip_Flop d_ff_1 (.D(multiplexer_1_out), .clk(sysclock), .Q(pc[3]), .reset(resetall));  // open: Qn, preset
  and and_2 (and_2_out, and_5_out, pc[7]);
  D_Flip_Flop d_ff_2 (.D(multiplexer_2_out), .clk(sysclock), .Q(pc[7]), .reset(resetall));  // open: Qn, preset
  // AND_Gate and_3 has open pins: in0=and_6_out, in1=pc[11], out=open
  xor xor_1 (xor_1_out, and_6_out, pc[11]);
  D_Flip_Flop d_ff_3 (.D(multiplexer_3_out), .clk(sysclock), .Q(pc[11]), .reset(resetall));  // open: Qn, preset
  xor xor_2 (xor_2_out, and_4_out, pc[3]);
  xor xor_3 (xor_3_out, and_5_out, pc[7]);
  Multiplexer #(.enable("false")) multiplexer_4 (.in0(xor_5_out), .in1(a[2]), .out(multiplexer_4_out), .sel(jmp));
  Multiplexer #(.enable("false")) multiplexer_5 (.in0(xor_4_out), .in1(a[10]), .out(multiplexer_5_out), .sel(jmp));
  and and_4 (and_4_out, and_7_out, pc[2]);
  D_Flip_Flop d_ff_4 (.D(multiplexer_4_out), .clk(sysclock), .Q(pc[2]), .reset(resetall));  // open: Qn, preset
  and and_5 (and_5_out, and_9_out, pc[6]);
  Multiplexer #(.enable("false")) multiplexer_6 (.in0(xor_6_out), .in1(a[6]), .out(multiplexer_6_out), .sel(jmp));
  D_Flip_Flop d_ff_5 (.D(multiplexer_6_out), .clk(sysclock), .Q(pc[6]), .reset(resetall));  // open: Qn, preset
  and and_6 (and_6_out, and_8_out, pc[10]);
  xor xor_4 (xor_4_out, and_8_out, pc[10]);
  D_Flip_Flop d_ff_6 (.D(multiplexer_5_out), .clk(sysclock), .Q(pc[10]), .reset(resetall));  // open: Qn, preset
  RAM #(.addrWidth(12), .dataWidth(25)) ram_1 (
    .addr(pc), .we(1'b0), .oe(1'b1), .clk(sysclock), .data({op, rd, rs1, rs2, imm}));
  xor xor_5 (xor_5_out, and_7_out, pc[2]);
  xor xor_6 (xor_6_out, and_9_out, pc[6]);
  and and_7 (and_7_out, and_10_out, pc[1]);
  Multiplexer #(.enable("false")) multiplexer_7 (.in0(xor_7_out), .in1(a[1]), .out(multiplexer_7_out), .sel(jmp));
  Multiplexer #(.enable("false")) multiplexer_8 (.in0(xor_8_out), .in1(a[5]), .out(multiplexer_8_out), .sel(jmp));
  and and_8 (and_8_out, and_11_out, pc[9]);
  Multiplexer #(.enable("false")) multiplexer_9 (.in0(xor_9_out), .in1(a[9]), .out(multiplexer_9_out), .sel(jmp));
  D_Flip_Flop d_ff_7 (.D(multiplexer_9_out), .clk(sysclock), .Q(pc[9]), .reset(resetall));  // open: Qn, preset
  xor xor_7 (xor_7_out, and_10_out, pc[1]);
  D_Flip_Flop d_ff_8 (.D(multiplexer_7_out), .clk(sysclock), .Q(pc[1]), .reset(resetall));  // open: Qn, preset
  and and_9 (and_9_out, and_12_out, pc[5]);
  xor xor_8 (xor_8_out, and_12_out, pc[5]);
  D_Flip_Flop d_ff_9 (.D(multiplexer_8_out), .clk(sysclock), .Q(pc[5]), .reset(resetall));  // open: Qn, preset
  xor xor_9 (xor_9_out, and_11_out, pc[9]);
  and and_10 (and_10_out, 1'b1, pc[0]);
  Multiplexer #(.enable("false")) multiplexer_10 (.in0(xor_10_out), .in1(a[0]), .out(multiplexer_10_out), .sel(jmp));
  Multiplexer #(.enable("false")) multiplexer_11 (.in0(xor_11_out), .in1(a[4]), .out(multiplexer_11_out), .sel(jmp));
  and and_11 (and_11_out, and_2_out, pc[8]);
  Multiplexer #(.enable("false")) multiplexer_12 (.in0(xor_12_out), .in1(a[8]), .out(multiplexer_12_out), .sel(jmp));
  D_Flip_Flop d_ff_10 (.D(multiplexer_12_out), .clk(sysclock), .Q(pc[8]), .reset(resetall));  // open: Qn, preset
  xor xor_10 (xor_10_out, 1'b1, pc[0]);
  D_Flip_Flop d_ff_11 (.D(multiplexer_10_out), .clk(sysclock), .Q(pc[0]), .reset(resetall));  // open: Qn, preset
  and and_12 (and_12_out, and_1_out, pc[4]);
  xor xor_11 (xor_11_out, and_1_out, pc[4]);
  D_Flip_Flop d_ff_12 (.D(multiplexer_11_out), .clk(sysclock), .Q(pc[4]), .reset(resetall));  // open: Qn, preset
  xor xor_12 (xor_12_out, and_2_out, pc[8]);

  // Other names for the same wires on the sheet: clk = sysclock; im0 = imm[0]; im1 = imm[1]; im2 = imm[2];
  //   im3 = imm[3]; im4 = imm[4]; im5 = imm[5]; im6 = imm[6]; im7 = imm[7]; im8 = imm[8]; im9 = imm[9];
  //   im10 = imm[10]; im11 = imm[11]; sc = resetall
endmodule

module regfile (
  input  [2:0] rd,
  input  [11:0] alur,
  input  [11:0] pc,
  input  [11:0] imm,
  input  [3:0] op,
  input  wen,
  input  resetall,
  input  sysclock,
  output [11:0] x0,
  output [11:0] x1,
  output [11:0] x2,
  output [11:0] x3,
  output [11:0] x4,
  output [11:0] x5,
  output [11:0] x6,
  output [11:0] x7
);

  wire demultiplexer_1_out0, demultiplexer_1_out1, demultiplexer_1_out2, demultiplexer_1_out3,
       demultiplexer_1_out4, demultiplexer_1_out5, demultiplexer_1_out6, demultiplexer_1_out7, reg0, reg1,
       reg2, reg3, reg4, reg5, reg6, reg7, s0, s1;
  wire [11:0] mux;

  Register #(.width(12)) register_1 (.D(mux), .en(demultiplexer_1_out0), .clk(reg0), .Q(x0), .clr(resetall));
  Register #(.width(12)) register_2 (.D(mux), .en(demultiplexer_1_out1), .clk(reg1), .Q(x1), .clr(resetall));
  Register #(.width(12)) register_3 (.D(mux), .en(demultiplexer_1_out2), .clk(reg2), .Q(x2), .clr(resetall));
  Register #(.width(12)) register_4 (.D(mux), .en(demultiplexer_1_out3), .clk(reg3), .Q(x3), .clr(resetall));
  Register #(.width(12)) register_5 (.D(mux), .en(demultiplexer_1_out4), .clk(reg4), .Q(x4), .clr(resetall));
  Register #(.width(12)) register_6 (.D(mux), .en(demultiplexer_1_out5), .clk(reg5), .Q(x5), .clr(resetall));
  Register #(.width(12)) register_7 (.D(mux), .en(demultiplexer_1_out6), .clk(reg6), .Q(x6), .clr(resetall));
  Register #(.width(12)) register_8 (.D(mux), .en(demultiplexer_1_out7), .clk(reg7), .Q(x7), .clr(resetall));
  and and_1 (s1, op[3], ~op[2], op[0]);  // AND_Gate
  and and_2 (reg0, ~rd[0], ~rd[1], ~rd[2], sysclock);  // AND_Gate
  and and_3 (reg1, rd[0], ~rd[1], ~rd[2], sysclock);  // AND_Gate
  and and_4 (reg2, ~rd[0], rd[1], ~rd[2], sysclock);  // AND_Gate
  and and_5 (s0, op[3], ~op[2], ~op[1], ~op[0]);  // AND_Gate
  and and_6 (reg3, rd[0], rd[1], ~rd[2], sysclock);  // AND_Gate
  and and_7 (reg4, ~rd[0], ~rd[1], rd[2], sysclock);  // AND_Gate
  and and_8 (reg5, rd[0], ~rd[1], rd[2], sysclock);  // AND_Gate
  Demultiplexer #(.select(3), .enable("false")) demultiplexer_1 (
    .out0(demultiplexer_1_out0), .out1(demultiplexer_1_out1), .out2(demultiplexer_1_out2),
    .out3(demultiplexer_1_out3), .out4(demultiplexer_1_out4), .out5(demultiplexer_1_out5),
    .out6(demultiplexer_1_out6), .out7(demultiplexer_1_out7), .in(wen), .sel(rd));
  Multiplexer #(.select(2), .width(12), .enable("false")) multiplexer_1 (
    .in0(alur), .in1(pc), .in2(imm), .out(mux), .sel({s1, s0}));  // open: in3
  and and_9 (reg6, ~rd[0], rd[1], rd[2], sysclock);  // AND_Gate
  and and_10 (reg7, rd[0], rd[1], rd[2], sysclock);

  // Other names for the same wires on the sheet: clk = sysclock; D = op[0]; C = op[1]; B = op[2]; A = op[3];
  //   q0[11:0] = x0; q1[11:0] = x1; q2[11:0] = x2; q3[11:0] = x3; q4[11:0] = x4; q5[11:0] = x5; q6[11:0] = x6;
  //   q7[11:0] = x7
endmodule
